# Fritzing sketch Head electronics (saved by Fritzing 0.9.6b)
breadboards: 1

parts:
  MCU1 = Raspberry Pi Zero
  NEOPIXEL2 = Neopixel Strip -- Black (60/m) [part_number=1461]
  NEOPIXEL3 = Neopixel Strip -- Black (60/m) [part_number=1461]
  SPKR1 = Loudspeaker  # not connected
  MIC1 = Microphone  # not connected
  Part5 = I2C level shifter bidirectional
  Mic1 = KY-038

nets:
  N1: MCU1.pin_1, MCU1.pin_17, Part5.LV, Mic1.pin3
  +5V: MCU1.pin_2, MCU1.pin_4, NEOPIXEL2.+5V, NEOPIXEL3.+5V, Part5.HV
  GND: MCU1.pin_6, MCU1.pin_34, MCU1.pin_39, NEOPIXEL2.GND, NEOPIXEL3.GND, Part5.GND, Mic1.pin2
  N2: MCU1.pin_8, Mic1.pin4
  N3: MCU1.pin_12, Part5.LV2
  N4: MCU1.pin_33, Part5.LV4
  N5: NEOPIXEL2.DI, NEOPIXEL3.DI, Part5.HV2

notes:
  USB sound card connects Pi to mic and speaker
  [0.5m]
  [0.3m]

custom parts:
  Neopixel Strip -- Black (60/m): Neopixel Strip, Black, 60 pixels per meter.
  KY-038: ky-038 Microphone sound sensor module
